# Fritzing sketch IRRemocon (saved by Fritzing 0.9.3b)
breadboards: 1

parts:
  Raspberry_Pi_1 = Raspberry Pi 3 [part_number=RPI-3-V1.2]
  IR1 = TSOP312.., 314.. [package=THT]
  LED1 = smd LED [color="Red (633nm)" package="0603 [SMD]"]
  R1 = Resistor [tolerance=±5% resistance=330 package=THT]
  S1 = Pushbutton [package="[THT]"]
  R2 = Resistor [tolerance=±5% resistance=330 package=THT]

nets:
  N1: Raspberry_Pi_1.3v3, IR1.Data, S1.Pin_1, S1.Pin_2
  N2: Raspberry_Pi_1.GIPO21, S1.Pin_3, S1.Pin_4, R2.Pin_1
  N3: Raspberry_Pi_1.GIPO16, R1.Pin_1
  N4: Raspberry_Pi_1.GIPO18, IR1.GND
  N5: Raspberry_Pi_1.GND, IR1.Vs, LED1.cathode, R2.Pin_0
  N6: LED1.anode, R1.Pin_0
